// Logisim project Сумматор.circ as structural Verilog: 1 circuit, main circuit main
module main (
  input  in_1,
  input  in_2,
  input  in_3,
  input  in_4,
  input  in_5,
  input  in_6,
  input  in_7,
  input  in_8,
  input  in_9,
  input  in_10,
  input  in_11,
  input  in_12,
  input  in_13,
  input  in_14,
  input  in_15,
  input  in_16,
  input  in_17,
  input  in_18,
  input  in_19,
  input  in_20,
  input  in_21,
  input  in_22,
  input  in_23,
  input  in_24,
  input  in_25,
  input  in_26,
  input  in_27,
  input  in_28,
  output out_29,
  output out_30,
  output out_31,
  output out_32,
  output out_33,
  output out_34,
  output out_35,
  output out_36,
  output P,
  output P_2,
  output out_39,
  output out_40,
  output out_41,
  output out_42,
  output P_3,
  output P_4,
  output out_45,
  output out_46,
  output out_47,
  output out_48,
  output out_49,
  output P_5,
  output P_6,
  output out_52,
  output out_53,
  output out_54,
  output out_55,
  output out_56,
  output P_7
);

  wire _0_2_out, _0_out, _1_2_out, _1_3_out, _1_4_out, _1_5_out, _1_out, _2_2_out, _2_3_out, _2_4_out,
       _2_5_out, _2_out, _3_2_out, _3_3_out, _3_4_out, _3_out, _4_2_out, _4_3_out, _4_4_out, _4_out,
       _5_2_out, _5_3_out, _5_4_out, _5_out, _6_2_out, _6_3_out, _6_4_out, _6_out, _7_2_out, _7_3_out,
       _7_4_out, _7_out, _8_2_out, _8_out, _9_2_out, _9_out, _10_out, _11_out, _12_out, _13_out, _14_out,
       _15_out, _16_out, _17_out, _18_out, _19_out, _20_out, _21_out, _22_out, _23_out, _24_out, _25_out,
       _26_out, _27_out, _28_out, _29_out, _30_out, and_7_out, and_8_out, and_9_out, and_10_out, and_11_out,
       and_12_out, and_13_out, and_14_out, and_15_out, and_16_out, and_17_out, and_18_out, and_19_out,
       and_20_out, and_21_out, and_22_out, and_27_out, and_28_out, and_29_out, and_30_out, and_31_out,
       and_32_out, and_33_out, and_34_out, and_35_out, and_36_out, and_37_out, and_38_out, and_39_out,
       and_40_out, and_41_out, and_42_out, nand_1_out, nand_2_out, nand_3_out, nand_4_out, nand_5_out,
       nand_6_out, nand_7_out, nand_8_out, nand_9_out, nand_10_out, nand_11_out, nand_12_out, nand_13_out,
       nand_16_out, nand_17_out, nand_18_out, nand_19_out, nand_20_out, nand_21_out, nand_23_out,
       nand_24_out, nor_1_out, nor_2_out, nor_3_out, nor_4_out, nor_5_out, nor_6_out, nor_7_out, nor_8_out,
       nor_9_out, nor_10_out, nor_11_out, not_1_out, not_2_out, not_3_out, not_4_out, not_5_out, or_1_out,
       or_3_out, or_4_out, or_5_out, or_6_out, or_7_out, or_9_out, or_11_out, or_13_out, or_15_out,
       or_16_out, or_17_out, or_18_out, or_19_out, or_20_out, or_21_out, or_22_out, or_23_out, or_25_out,
       or_27_out, or_29_out, or_31_out, or_33_out, or_34_out;

  nand nand_1 (nand_1_out, in_1, in_2);
  nor nor_1 (nor_1_out, in_1, in_2);
  or or_1 (or_1_out, in_1, in_2);
  nand nand_2 (nand_2_out, in_1, in_2);
  nand nand_3 (nand_3_out, in_18, in_15);
  nand nand_4 (nand_4_out, in_19, in_16);
  nand nand_5 (nand_5_out, in_20, in_17);
  nand nand_6 (nand_6_out, in_1, nand_1_out);
  nand nand_7 (nand_7_out, nand_1_out, in_2);
  nor nor_2 (nor_2_out, in_1, nor_1_out);
  nor nor_3 (nor_3_out, nor_1_out, in_2);
  nand nand_8 (nand_8_out, in_18, nand_3_out);
  nand nand_9 (nand_9_out, nand_3_out, in_15);
  nand nand_10 (nand_10_out, in_19, nand_4_out);
  nand nand_11 (nand_11_out, nand_4_out, in_16);
  nand nand_12 (nand_12_out, in_20, nand_5_out);
  nand nand_13 (nand_13_out, nand_5_out, in_17);
  and and_1 (out_35, or_1_out, nand_2_out);
  and and_2 (out_45, in_18, in_15);
  nand nand_14 (out_29, nand_6_out, nand_7_out);
  and and_3 (out_30, in_1, in_2);
  or or_2 (out_33, nor_2_out, nor_3_out);
  nand nand_15 (out_42, nand_8_out, nand_9_out);
  nand nand_16 (nand_16_out, nand_10_out, nand_11_out);
  nand nand_17 (nand_17_out, nand_12_out, nand_13_out);
  and and_4 (out_54, in_20, in_17);
  and and_5 (out_48, nand_16_out, out_45);
  nand nand_18 (nand_18_out, out_45, nand_16_out);
  nand nand_19 (nand_19_out, out_45, nand_18_out);
  nand nand_20 (nand_20_out, nand_18_out, nand_16_out);
  nand nand_21 (nand_21_out, out_48, nand_17_out);
  and and_6 (out_53, nand_17_out, out_48);
  nand nand_22 (out_46, nand_19_out, nand_20_out);
  nand nand_23 (nand_23_out, out_48, nand_21_out);
  nand nand_24 (nand_24_out, nand_21_out, nand_17_out);
  nand nand_25 (out_49, nand_23_out, nand_24_out);
  and and_7 (and_7_out, in_7, in_8);
  or or_3 (or_3_out, in_7, in_8);
  and and_8 (and_8_out, in_13, in_14);
  or or_4 (or_4_out, in_13, in_14);
  and and_9 (and_9_out, in_23, in_24);
  or or_5 (or_5_out, in_23, in_24);
  and and_10 (and_10_out, in_27, in_28);
  or or_6 (or_6_out, in_27, in_28);
  and and_11 (and_11_out, or_3_out, in_9);
  and and_12 (and_12_out, or_4_out, P_2);
  and and_13 (and_13_out, or_5_out, P_4);
  and and_14 (and_14_out, or_6_out, P_6);
  and and_15 (and_15_out, and_7_out, in_9);
  or or_7 (or_7_out, in_9, or_3_out);
  or or_8 (P_2, and_11_out, and_7_out);
  and and_16 (and_16_out, and_8_out, P_2);
  or or_9 (or_9_out, P_2, or_4_out);
  or or_10 (P_4, and_12_out, and_8_out);
  and and_17 (and_17_out, and_9_out, P_4);
  or or_11 (or_11_out, P_4, or_5_out);
  or or_12 (P_6, and_13_out, and_9_out);
  and and_18 (and_18_out, and_10_out, P_6);
  or or_13 (or_13_out, P_6, or_6_out);
  or or_14 (P_7, and_14_out, and_10_out);
  not nor_4 (nor_4_out, P_2);  // NOR_Gate
  not nor_5 (nor_5_out, P_4);  // NOR_Gate
  not nor_6 (nor_6_out, P_6);  // NOR_Gate
  not nor_7 (nor_7_out, P_7);  // NOR_Gate
  and and_19 (and_19_out, or_7_out, nor_4_out);
  and and_20 (and_20_out, or_9_out, nor_5_out);
  and and_21 (and_21_out, or_11_out, nor_6_out);
  and and_22 (and_22_out, or_13_out, nor_7_out);
  or or_15 (or_15_out, and_15_out, and_19_out);
  or or_16 (or_16_out, and_16_out, and_20_out);
  or or_17 (or_17_out, and_17_out, and_21_out);
  or or_18 (or_18_out, and_18_out, and_22_out);
  and and_23 (out_34, or_15_out, in_10);
  and and_24 (out_40, or_16_out, in_10);
  and and_25 (out_47, or_17_out, in_10);
  and and_26 (out_55, or_18_out, in_10);
  or or_19 (or_19_out, in_3, in_4);
  or or_20 (or_20_out, in_11, in_12);
  or or_21 (or_21_out, in_21, in_22);
  or or_22 (or_22_out, in_25, in_26);
  and and_27 (and_27_out, in_3, in_4);
  and and_28 (and_28_out, or_19_out, in_5);
  and and_29 (and_29_out, in_11, in_12);
  and and_30 (and_30_out, or_20_out, P);
  and and_31 (and_31_out, in_21, in_22);
  and and_32 (and_32_out, or_21_out, P_3);
  and and_33 (and_33_out, in_25, in_26);
  and and_34 (and_34_out, or_22_out, P_5);
  and and_35 (and_35_out, and_27_out, in_5);
  or or_23 (or_23_out, in_5, or_19_out);
  or or_24 (P, and_28_out, and_27_out);
  and and_36 (and_36_out, and_29_out, P);
  or or_25 (or_25_out, P, or_20_out);
  or or_26 (P_3, and_30_out, and_29_out);
  and and_37 (and_37_out, and_31_out, P_3);
  or or_27 (or_27_out, P_3, or_21_out);
  or or_28 (P_5, and_32_out, and_31_out);
  and and_38 (and_38_out, and_33_out, P_5);
  or or_29 (or_29_out, P_5, or_22_out);
  or or_30 (out_56, and_34_out, and_33_out);
  not nor_8 (nor_8_out, P);  // NOR_Gate
  not nor_9 (nor_9_out, P_3);  // NOR_Gate
  not nor_10 (nor_10_out, P_5);  // NOR_Gate
  not nor_11 (nor_11_out, out_56);  // NOR_Gate
  and and_39 (and_39_out, or_23_out, nor_8_out);
  and and_40 (and_40_out, or_25_out, nor_9_out);
  and and_41 (and_41_out, or_27_out, nor_10_out);
  and and_42 (and_42_out, or_29_out, nor_11_out);
  or or_31 (or_31_out, and_35_out, and_39_out);
  or or_32 (out_39, and_36_out, and_40_out);
  or or_33 (or_33_out, and_37_out, and_41_out);
  or or_34 (or_34_out, and_38_out, and_42_out);
  and and_43 (out_41, or_33_out, in_6);
  and and_44 (out_52, or_34_out, in_6);
  and and_45 (out_32, or_31_out, in_6);
  and and_46 (out_31, out_39, in_6);
  not not_1 (not_1_out, out_31);
  not not_2 (not_2_out, out_32);
  not not_3 (not_3_out, out_41);
  not not_4 (not_4_out, out_52);
  not not_5 (not_5_out, out_56);
  and _1 (_1_out, out_32, not_1_out, not_3_out, not_4_out, not_5_out);
  and _2 (_2_out, out_31, not_2_out, not_3_out, not_4_out, not_5_out);
  and _3 (_3_out, out_32, out_31, not_3_out, not_4_out, not_5_out);
  and _4 (_4_out, out_41, not_2_out, not_1_out, not_4_out, not_5_out);
  and _5 (_5_out, out_32, out_41, not_1_out, not_4_out, not_5_out);
  and _6 (_6_out, out_31, out_41, not_2_out, not_4_out, not_5_out);
  and _7 (_7_out, out_32, out_31, out_41, not_4_out, not_5_out);
  and _8 (_8_out, out_52, not_2_out, not_1_out, not_3_out, not_5_out);
  and _9 (_9_out, out_32, out_52, not_1_out, not_3_out, not_5_out);
  and _10 (_10_out, out_52, out_31, not_2_out, not_3_out, not_5_out);
  and _11 (_11_out, out_32, out_31, out_52, not_3_out, not_5_out);
  and _12 (_12_out, out_41, out_52, not_2_out, not_1_out, not_5_out);
  and _13 (_13_out, out_32, out_41, out_52, not_1_out, not_5_out);
  and _14 (_14_out, out_31, out_41, out_52, not_2_out, not_5_out);
  and _15 (_15_out, out_32, out_31, out_41, out_52, not_5_out);
  and _16 (_16_out, out_56, not_2_out, not_1_out, not_3_out, not_4_out);
  and _17 (_17_out, out_32, out_56, not_1_out, not_3_out, not_4_out);
  and _18 (_18_out, out_31, out_56, not_2_out, not_3_out, not_4_out);
  and _19 (_19_out, out_32, out_31, out_56, not_3_out, not_4_out);
  and _20 (_20_out, out_41, out_56, not_2_out, not_1_out, not_4_out);
  and _21 (_21_out, out_32, out_41, out_56);
  and _22 (_22_out, out_31, out_41, out_56, not_2_out, not_4_out);
  and _23 (_23_out, out_32, out_31, out_41, out_56, not_4_out);
  and _24 (_24_out, out_52, out_56, not_2_out, not_1_out, not_3_out);
  and _25 (_25_out, out_32, out_52, out_56, not_1_out, not_3_out);
  and _26 (_26_out, out_31, out_52, out_56, not_2_out, not_3_out);
  and _27 (_27_out, out_32, out_31, out_52, out_56, not_3_out);
  and _28 (_28_out, out_41, out_52, out_56, not_2_out, not_1_out);
  and _29 (_29_out, out_32, out_41, out_52, out_56, not_1_out);
  and _30 (_30_out, out_31, out_41, out_52, out_56, not_2_out);
  and _0 (_0_out, not_2_out, not_1_out, not_3_out, not_4_out, not_5_out);
  or _0_2 (_0_2_out, _0_out, _10_out, _20_out, _30_out);
  or _1_2 (_1_2_out, _1_out, _11_out, _21_out);
  or _2_2 (_2_2_out, _2_out, _12_out, _22_out);
  or _3_2 (_3_2_out, _3_out, _13_out, _23_out);
  or _4_2 (_4_2_out, _4_out, _14_out, _24_out);
  or _5_2 (_5_2_out, _5_out, _15_out, _25_out);
  or _6_2 (_6_2_out, _6_out, _16_out, _26_out);
  or _7_2 (_7_2_out, _7_out, _17_out, _27_out);
  or _8_2 (_8_2_out, _8_out, _18_out, _28_out);
  or _9_2 (_9_2_out, _9_out, _19_out, _29_out);
  or _1_3 (_1_3_out, _10_out, _11_out, _12_out, _13_out, _14_out, _15_out, _16_out, _17_out, _18_out, _19_out);
  or _2_3 (_2_3_out, _20_out, _21_out, _22_out, _23_out, _24_out, _25_out, _26_out, _27_out, _28_out, _29_out);
  or _7_3 (_7_3_out, _2_2_out, _3_2_out, _4_2_out, _5_2_out, _6_2_out, _8_2_out, _9_2_out);
  or _6_3 (_6_3_out, _0_2_out, _4_2_out, _5_2_out, _6_2_out, _8_2_out, _9_2_out);
  or _1_4 (_1_4_out, _0_2_out, _2_2_out, _3_2_out, _5_2_out, _6_2_out, _7_2_out, _8_2_out, _9_2_out);
  or _2_4 (_2_4_out, _0_2_out, _1_2_out, _2_2_out, _3_2_out, _4_2_out, _7_2_out, _8_2_out, _9_2_out);
  or _5_3 (_5_3_out, _0_2_out, _2_2_out, _6_2_out, _8_2_out);
  or _4_3 (_4_3_out, _5_2_out, _0_2_out, _2_2_out, _3_2_out, _6_2_out, _8_2_out, _9_2_out);
  or _3_3 (_3_3_out, _0_2_out, _1_2_out, _3_2_out, _4_2_out, _5_2_out, _6_2_out, _7_2_out, _8_2_out, _9_2_out);
  or _2_5 (_2_5_out, _1_3_out, _2_3_out, _30_out);
  or _1_5 (_1_5_out, _2_3_out, _30_out);
  // OR_Gate _6_4 has open pins: out=_6_4_out
  or _7_4 (_7_4_out, _2_3_out, _30_out);
  buf _5_4 (_5_4_out, _2_3_out);  // OR_Gate
  or _4_4 (_4_4_out, _2_3_out, _30_out);
  or _3_4 (_3_4_out, _1_3_out, _30_out);
  _7_Segment_Display u_7_segment_display_1 (
    .g(_7_4_out), .f(_6_4_out), .a(_1_5_out), .b(_2_5_out), .e(_5_4_out), .d(_4_4_out), .c(_3_4_out));  // open: dp
  _7_Segment_Display u_7_segment_display_2 (
    .g(_7_3_out), .f(_6_3_out), .a(_1_4_out), .b(_2_4_out), .e(_5_3_out), .d(_4_3_out), .c(_3_3_out));  // open: dp

  assign out_36 = out_31;

  // Notes on the sheet:
  //   S
  //   S
  //   S
  //   S
  //   S
  //   S
  //   S
  //   S
  //          P
  //   0
  //   4
  //   3
  //   1
  //   2
  //   13
  //   9
  //   11
  //   5
  //   6
  //   8
  //   7
  //   12
  //   10
  //   17
  //   19
  //   15
  //   16
  //   14
  //   18
  //   20
  //   29
  //   25
  //   27
  //   23
  //   21
  //   28
  //   26
  //   22
  //   24
  //   30
  //   0
  //   2
  //   1
  //   3
  //   4
  //   7
  //   6
  //   8
  //   5
  //   3
  //   9
endmodule
