// Logisim project синхронизированные SR-триггеры.circ as structural Verilog: 1 circuit, main circuit main
module main (
  input  s,
  input  r,
  input  c,
  input  _0,
  input  _1,
  input  _2,
  input  _3,
  input  _4,
  input  _5,
  input  _6,
  input  _7,
  input  _8,
  input  _9,
  input  _10,
  input  _11,
  input  _12,
  input  _13,
  input  _14,
  input  _15,
  input  _16,
  input  _17,
  input  _18,
  input  _19,
  input  _20,
  input  _21,
  input  _22,
  input  _23,
  input  _24,
  input  _25,
  input  _26,
  input  _27,
  input  _28,
  input  _29,
  input  _30,
  input  _31,
  input  s_2,
  input  r_2,
  input  c_2,
  input  _0_2,
  input  _1_2,
  input  _2_2,
  input  _3_2,
  input  _4_2,
  input  _5_2,
  input  _6_2,
  input  _7_2,
  input  _8_2,
  input  _9_2,
  input  _10_2,
  input  _11_2,
  input  _12_2,
  input  _13_2,
  input  _14_2,
  input  _15_2,
  input  in_55,
  output out_56,
  output out_57,
  output out_58,
  output out_59
);

  wire _0_2_out, _0_3_out, _0_4_out, _0_out, _1_2_out, _1_3_out, _1_4_out, _1_5_out, _1_6_out, _1_7_out,
       _1_8_out, _1_9_out, _1_10_out, _1_11_out, _1_12_out, _1_out, _2_2_out, _2_3_out, _2_4_out, _2_5_out,
       _2_6_out, _2_7_out, _2_8_out, _2_9_out, _2_10_out, _2_11_out, _2_out, _3_2_out, _3_3_out, _3_4_out,
       _3_5_out, _3_6_out, _3_7_out, _3_8_out, _3_9_out, _3_out, _4_2_out, _4_3_out, _4_4_out, _4_5_out,
       _4_6_out, _4_7_out, _4_8_out, _4_9_out, _4_10_out, _4_out, _5_2_out, _5_3_out, _5_4_out, _5_5_out,
       _5_6_out, _5_7_out, _5_8_out, _5_out, _6_2_out, _6_3_out, _6_4_out, _6_5_out, _6_6_out, _6_7_out,
       _6_8_out, _6_out, _7_2_out, _7_3_out, _7_4_out, _7_5_out, _7_6_out, _7_7_out, _7_8_out, _7_out,
       _8_2_out, _8_3_out, _8_4_out, _8_5_out, _8_6_out, _8_out, _9_2_out, _9_3_out, _9_4_out, _9_out,
       _10_2_out, _10_out, _11_2_out, _11_out, _12_2_out, _12_out, _13_2_out, _13_out, _14_2_out, _14_out,
       _15_2_out, _15_out, _16_2_out, _16_out, _17_out, _18_out, _19_out, _20_out, _21_out, _22_out, _23_out,
       _24_out, _25_out, _26_out, _27_out, _28_out, _29_out, _30_out, _31_out, and_1_out, and_2_out,
       and_3_out, and_4_out, and_5_out, and_6_out, and_7_out, and_8_out, and_9_out, and_10_out, and_11_out,
       and_12_out, and_13_out, and_14_out, and_15_out, and_16_out, and_17_out, and_18_out, and_19_out,
       and_20_out, and_21_out, and_22_out, and_23_out, and_24_out, and_25_out, and_26_out, not_1_out,
       not_2_out, not_3_out, not_4_out, not_5_out, not_6_out, not_9_out, not_10_out, not_11_out, not_12_out,
       not_13_out, not_14_out, not_15_out;

  and and_1 (and_1_out, s_2, c_2);
  and and_2 (and_2_out, r_2, c_2);
  or u__1 (_1_out, _1_2, _3_2, _5_2, _7_2, _9_2, _11_2, _13_2, _15_2);
  or u__2 (_2_out, _2_2, _3_2, _6_2, _7_2, _10_2, _11_2, _14_2, _15_2);
  or u__4 (_4_out, _4_2, _5_2, _6_2, _7_2, _12_2, _13_2, _14_2, _15_2);
  or u__8 (_8_out, _8_2, _9_2, _10_2, _11_2, _12_2, _13_2, _14_2, _15_2);
  not not_1 (not_1_out, and_1_out);
  not not_2 (not_2_out, and_2_out);
  not not_3 (not_3_out, _1_out);
  not not_4 (not_4_out, _2_out);
  not not_5 (not_5_out, _4_out);
  not not_6 (not_6_out, _8_out);
  not not_7 (out_57, and_3_out);
  and and_3 (and_3_out, not_1_out, out_59);
  not not_8 (out_59, and_4_out);
  and and_4 (and_4_out, out_57, not_2_out);
  and u__0 (_0_out, not_3_out, not_4_out, not_5_out, not_6_out);
  and u__1_2 (_1_2_out, _1_out, not_4_out, not_5_out, not_6_out);
  and u__2_2 (_2_2_out, _2_out, not_3_out, not_5_out, not_6_out);
  and u__3 (_3_out, _1_out, _2_out, not_5_out, not_6_out);
  and u__4_2 (_4_2_out, _4_out, not_3_out, not_4_out, not_6_out);
  and u__5 (_5_out, _1_out, _4_out, not_4_out, not_6_out);
  and u__6 (_6_out, _2_out, _4_out, not_3_out, not_6_out);
  and u__7 (_7_out, _1_out, _2_out, _4_out, not_6_out);
  and u__8_2 (_8_2_out, _8_out, not_3_out, not_4_out, not_5_out);
  and u__9 (_9_out, _1_out, _8_out, not_4_out, not_5_out);
  and u__10 (_10_out, _2_out, _8_out, not_3_out, not_5_out);
  and u__11 (_11_out, _1_out, _2_out, _8_out, not_5_out);
  and u__12 (_12_out, _4_out, _8_out, not_3_out, not_4_out);
  and u__13 (_13_out, _1_out, _4_out, _8_out, not_4_out);
  and u__14 (_14_out, _2_out, _4_out, _8_out, not_3_out);
  and u__15 (_15_out, _1_out, _2_out, _4_out, _8_out);
  or u__0_2 (_0_2_out, _0_out, _10_out);
  or _1_3 (_1_3_out, _1_2_out, _11_out);
  or _2_3 (_2_3_out, _2_2_out, _12_out);
  or u__3_2 (_3_2_out, _3_out, _13_out);
  or _4_3 (_4_3_out, _4_2_out, _14_out);
  or u__5_2 (_5_2_out, _5_out, _15_out);
  buf u__6_2 (_6_2_out, _6_out);  // OR_Gate
  buf u__7_2 (_7_2_out, _7_out);  // OR_Gate
  buf _8_3 (_8_3_out, _8_2_out);  // OR_Gate
  buf u__9_2 (_9_2_out, _9_out);  // OR_Gate
  or _1_4 (_1_4_out, _10_out, _11_out, _12_out, _13_out, _14_out, _15_out);
  or _2_4 (_2_4_out, _0_2_out, _1_3_out, _2_3_out, _3_2_out, _4_3_out, _7_2_out, _8_3_out, _9_2_out);
  or _1_5 (_1_5_out, _0_2_out, _2_3_out, _3_2_out, _5_2_out, _6_2_out, _7_2_out, _8_3_out, _9_2_out);
  or _6_3 (_6_3_out, _0_2_out, _4_3_out, _5_2_out, _6_2_out, _8_3_out, _9_2_out);
  or _7_3 (_7_3_out, _2_3_out, _3_2_out, _4_3_out, _5_2_out, _6_2_out, _8_3_out, _9_2_out);
  or _3_3 (_3_3_out, _0_2_out, _7_2_out, _1_3_out, _3_2_out, _4_3_out, _5_2_out, _6_2_out, _8_3_out, _9_2_out);
  or _4_4 (_4_4_out, _0_2_out, _2_3_out, _3_2_out, _5_2_out, _8_3_out, _6_2_out, _9_2_out);
  or _5_3 (_5_3_out, _0_2_out, _2_3_out, _6_2_out, _8_3_out);
  and and_5 (and_5_out, _2_4_out, out_57);
  and and_6 (and_6_out, _1_5_out, out_57);
  and and_7 (and_7_out, _6_3_out, out_57);
  and and_8 (and_8_out, _7_3_out, out_57);
  and and_9 (and_9_out, _3_3_out, out_57);
  and and_10 (and_10_out, _4_4_out, out_57);
  and and_11 (and_11_out, _5_3_out, _5_3_out, out_57);
  and and_12 (and_12_out, _1_4_out, out_57);
  buf _2_5 (_2_5_out, and_12_out);  // OR_Gate
  // OR_Gate _1_6 has open pins: out=_1_6_out
  // OR_Gate _6_4 has open pins: out=_6_4_out
  // OR_Gate _7_4 has open pins: out=_7_4_out
  buf _3_4 (_3_4_out, and_12_out);  // OR_Gate
  // OR_Gate _4_5 has open pins: out=_4_5_out
  // OR_Gate _5_4 has open pins: out=_5_4_out
  _7_Segment_Display u_7_segment_display_1 (
    .g(_7_4_out), .f(_6_4_out), .a(_1_6_out), .b(_2_5_out), .e(_5_4_out), .d(_4_5_out), .c(_3_4_out));  // open: dp
  _7_Segment_Display u_7_segment_display_2 (
    .g(and_8_out), .f(and_7_out), .a(and_6_out), .b(and_5_out), .e(and_11_out), .d(and_10_out), .c(and_9_out));  // open: dp
  and and_13 (and_13_out, s, c);
  and and_14 (and_14_out, r, c);
  or _1_7 (_1_7_out, _17, _19, _21, _23, _1, _3, _5, _7, _9, _11, _13, _15, _25, _27, _29, _31);
  or _2_6 (_2_6_out, _18, _22, _26, _30, _2, _3, _6, _7, _11, _14, _15, _19, _10, _23, _27, _31);
  or _4_6 (_4_6_out, _20, _21, _22, _23, _4, _5, _6, _7, _12, _13, _14, _15, _28, _29, _30, _31);
  or _8_4 (_8_4_out, _24, _25, _26, _27, _8, _9, _10, _11, _12, _13, _14, _15, _28, _29, _30, _31);
  or u__16 (_16_out, _16, _17, _18, _19, _20, _21, _22, _23, _24, _25, _26, _27, _28, _29, _30, _31);
  not not_9 (not_9_out, and_13_out);
  not not_10 (not_10_out, and_14_out);
  not not_11 (not_11_out, _1_7_out);
  not not_12 (not_12_out, _2_6_out);
  not not_13 (not_13_out, _4_6_out);
  not not_14 (not_14_out, _8_4_out);
  and and_15 (and_15_out, not_9_out, out_58);
  and and_16 (and_16_out, out_56, not_10_out);
  not not_15 (not_15_out, _16_out);
  not not_16 (out_56, and_15_out);
  not not_17 (out_58, and_16_out);
  and _0_3 (_0_3_out, not_11_out, not_12_out, not_13_out, not_14_out, not_15_out);
  and _1_8 (_1_8_out, _1_7_out, not_12_out, not_13_out, not_14_out, not_15_out);
  and _2_7 (_2_7_out, _2_6_out, not_11_out, not_13_out, not_14_out, not_15_out);
  and _3_5 (_3_5_out, _1_7_out, not_15_out, _2_6_out, not_13_out, not_14_out);
  and _4_7 (_4_7_out, _4_6_out, not_11_out, not_12_out, not_14_out, not_15_out);
  and _5_5 (_5_5_out, _1_7_out, _4_6_out, not_12_out, not_14_out, not_15_out);
  and _6_5 (_6_5_out, _2_6_out, _4_6_out, not_11_out, not_14_out, not_15_out);
  and _7_5 (_7_5_out, not_15_out, _1_7_out, _2_6_out, _4_6_out, not_14_out);
  and _8_5 (_8_5_out, _8_4_out, not_11_out, not_12_out, not_13_out, not_15_out);
  and _9_3 (_9_3_out, _1_7_out, _8_4_out, not_12_out, not_13_out, not_15_out);
  and u__10_2 (_10_2_out, _2_6_out, _8_4_out, not_11_out, not_13_out, not_15_out);
  and u__11_2 (_11_2_out, _1_7_out, _2_6_out, _8_4_out, not_13_out, not_15_out);
  and u__12_2 (_12_2_out, _4_6_out, _8_4_out, not_11_out, not_12_out, not_15_out);
  and u__13_2 (_13_2_out, _1_7_out, _4_6_out, _8_4_out, not_12_out, not_15_out);
  and u__14_2 (_14_2_out, _2_6_out, _4_6_out, _8_4_out, not_11_out, not_15_out);
  and u__15_2 (_15_2_out, _1_7_out, _2_6_out, _4_6_out, _8_4_out, not_15_out);
  and _16_2 (_16_2_out, _16_out, not_11_out, not_12_out, not_13_out, not_14_out);
  and u__17 (_17_out, _1_7_out, _16_out, not_12_out, not_13_out, not_14_out);
  and u__18 (_18_out, _2_6_out, _16_out, not_11_out, not_13_out, not_14_out);
  and u__19 (_19_out, _1_7_out, _2_6_out, _16_out, not_13_out, not_14_out);
  and u__20 (_20_out, _4_6_out, _16_out, not_11_out, not_12_out, not_14_out);
  and u__21 (_21_out, _1_7_out, _4_6_out, _16_out, not_12_out, not_14_out);
  and u__22 (_22_out, _2_6_out, _4_6_out, _16_out, not_11_out, not_14_out);
  and u__23 (_23_out, _1_7_out, _2_6_out, _4_6_out, _16_out, not_14_out);
  and u__24 (_24_out, _8_4_out, _16_out, not_11_out, not_12_out, not_13_out);
  and u__25 (_25_out, _1_7_out, _8_4_out, _16_out, not_12_out, not_13_out);
  and u__26 (_26_out, _2_6_out, _8_4_out, _16_out, not_11_out, not_13_out);
  and u__27 (_27_out, _1_7_out, _2_6_out, _8_4_out, _16_out, not_13_out);
  and u__28 (_28_out, _4_6_out, _8_4_out, _16_out, not_11_out, not_12_out);
  and u__29 (_29_out, _1_7_out, _4_6_out, _8_4_out, _16_out, not_12_out);
  and u__30 (_30_out, _2_6_out, _4_6_out, _8_4_out, _16_out, not_11_out);
  and u__31 (_31_out, _1_7_out, _2_6_out, _4_6_out, _8_4_out, _16_out);
  or _2_8 (_2_8_out, _20_out, _21_out, _22_out, _23_out, _24_out, _25_out, _26_out, _27_out, _28_out, _29_out);
  or _3_6 (_3_6_out, _30_out, _31_out);
  or _0_4 (_0_4_out, _0_3_out, _10_2_out, _20_out, _30_out);
  or _1_9 (_1_9_out, _1_8_out, _11_2_out, _22_out, _31_out);
  or _2_9 (_2_9_out, _2_7_out, _12_2_out, _22_out);
  or _3_7 (_3_7_out, _3_5_out, _13_2_out, _23_out);
  or _4_8 (_4_8_out, _4_7_out, _14_2_out, _24_out);
  or _5_6 (_5_6_out, _5_5_out, _15_2_out, _25_out);
  or _6_6 (_6_6_out, _6_5_out, _26_out);
  or _7_6 (_7_6_out, _7_5_out, _27_out);
  or _8_6 (_8_6_out, _8_5_out, _28_out);
  or _9_4 (_9_4_out, _9_3_out, _29_out);
  or _1_10 (_1_10_out, _10_2_out, _11_2_out, _12_2_out, _13_2_out, _14_2_out, _15_2_out, _16_2_out, _17_out, _18_out, _19_out);
  or _2_10 (_2_10_out, _0_4_out, _1_9_out, _2_9_out, _3_7_out, _4_8_out, _7_6_out, _8_6_out, _9_4_out);
  or _1_11 (_1_11_out, _0_4_out, _2_9_out, _3_7_out, _5_6_out, _6_6_out, _7_6_out, _8_6_out, _9_4_out);
  or _6_7 (_6_7_out, _0_4_out, _4_8_out, _5_6_out, _6_6_out, _8_6_out, _9_4_out);
  or _7_7 (_7_7_out, _2_9_out, _3_7_out, _4_8_out, _5_6_out, _6_6_out, _8_6_out, _9_4_out);
  or _3_8 (_3_8_out, _0_4_out, _7_6_out, _1_9_out, _3_7_out, _4_8_out, _5_6_out, _6_6_out, _8_6_out, _9_4_out);
  or _4_9 (_4_9_out, _0_4_out, _2_9_out, _3_7_out, _5_6_out, _8_6_out, _6_6_out, _9_4_out);
  or _5_7 (_5_7_out, _0_4_out, _2_9_out, _6_6_out, _8_6_out);
  and and_17 (and_17_out, _2_10_out, out_56);
  and and_18 (and_18_out, _1_11_out, out_56);
  and and_19 (and_19_out, _6_7_out, out_56);
  and and_20 (and_20_out, _1_10_out, out_56);
  and and_21 (and_21_out, out_56, _2_8_out);
  and and_22 (and_22_out, out_56, _3_6_out);
  and and_23 (and_23_out, _7_7_out, out_56);
  and and_24 (and_24_out, _3_8_out, out_56);
  and and_25 (and_25_out, _4_9_out, out_56);
  and and_26 (and_26_out, _5_7_out, _5_7_out, out_56);
  or _2_11 (_2_11_out, and_20_out, and_21_out, and_22_out);
  or _1_12 (_1_12_out, and_21_out, and_22_out);
  // OR_Gate _6_8 has open pins: out=_6_8_out
  or _7_8 (_7_8_out, and_21_out, and_22_out);
  or _3_9 (_3_9_out, and_20_out, and_22_out);
  or _4_10 (_4_10_out, and_21_out, and_22_out);
  buf _5_8 (_5_8_out, and_21_out);  // OR_Gate
  _7_Segment_Display u_7_segment_display_3 (
    .g(_7_8_out), .f(_6_8_out), .a(_1_12_out), .b(_2_11_out), .e(_5_8_out), .d(_4_10_out), .c(_3_9_out));  // open: dp
  _7_Segment_Display u_7_segment_display_4 (
    .g(and_23_out), .f(and_19_out), .a(and_18_out), .b(and_17_out), .e(and_26_out), .d(and_25_out),
    .c(and_24_out));  // open: dp

  // Notes on the sheet:
  //   0
  //   2
  //   1
  //   5
  //   3
  //   4
  //   6
  //   7
  //   9
  //   8
  //   10
  //   11
  //   12
  //   13
  //   14
  //   15
  //   0
  //   2
  //   1
  //   3
  //   4
  //   5
  //   7
  //   9
  //   8
  //   6
  //   0
  //   3
  //   2
  //   1
  //   4
  //   6
  //   7
  //   5
  //   8
  //   11
  //   9
  //   10
  //   12
  //   16
  //   14
  //   15
  //   13
  //   17
  //   19
  //   18
  //   20
  //   23
  //   24
  //   22
  //   21
  //   26
  //   25
  //   27
  //   28
  //   31
  //   29
  //   30
  //   2
  //   0
  //   1
  //   3
  //   5
  //   4
  //   6
  //   7
  //   9
  //   8
endmodule
